// Logisim project 1.a.circ as structural Verilog: 1 circuit, main circuit main
module main (
  input  a,
  input  b,
  output out_3
);

  wire not_1_out, not_2_out, or_out;

  not not_1 (not_1_out, a);
  not not_2 (not_2_out, b);
  or \or  (or_out, not_1_out, not_2_out);
  not not_3 (out_3, or_out);
endmodule
