// Logisim project 1.b.circ as structural Verilog: 1 circuit, main circuit main
module main (
  input  A,
  input  B,
  output out_3
);

  wire AND_out, not_1_out, not_2_out;

  not not_1 (not_1_out, A);
  not not_2 (not_2_out, B);
  and AND (AND_out, not_1_out, not_2_out);
  not not_3 (out_3, AND_out);
endmodule
