// Logisim project 2.a.circ as structural Verilog: 1 circuit, main circuit main
module main (
  input  A,
  input  B,
  input  C,
  output T
);

  wire AB_out, AC_out, BC_out;

  or AB (AB_out, A, B);
  or AC (AC_out, A, C);
  or BC (BC_out, B, C);
  and and_1 (T, AB_out, AC_out, BC_out);
endmodule
