// Logisim project 2.b.circ as structural Verilog: 1 circuit, main circuit main
module main (
  input  A,
  input  B,
  input  C,
  output out_4
);

  wire A_nB_nC_out, ABC_out, nA_B_nC_out, nA_nB_C_out;

  or nA_nB_C (nA_nB_C_out, ~A, ~B, C);  // OR_Gate
  or nA_B_nC (nA_B_nC_out, ~A, B, ~C);  // OR_Gate
  or A_nB_nC (A_nB_nC_out, A, ~B, ~C);  // OR_Gate
  or ABC (ABC_out, A, B, C);
  and S (out_4, nA_nB_C_out, nA_B_nC_out, A_nB_nC_out, ABC_out);
endmodule
