// Logisim project 4.circ as structural Verilog: 1 circuit, main circuit main
module main (
  input  D0,
  input  D1,
  input  D2,
  input  D3,
  input  S0,
  input  S1,
  output Y
);

  wire nand_1_out, nand_2_out, nand_3_out, nand_4_out, nand_5_out, nand_6_out, nand_7_out, nand_8_out,
       nand_9_out, nand_10_out, nand_11_out, nand_12_out, nand_13_out;

  nand nand_1 (nand_1_out, D0, D0);
  nand nand_2 (nand_2_out, D1, D1);
  nand nand_3 (nand_3_out, S0, S0);
  nand nand_4 (nand_4_out, D2, D2);
  nand nand_5 (nand_5_out, S1, S1);
  nand nand_6 (nand_6_out, D3, D3);
  nand nand_7 (nand_7_out, S1, S1);
  nand nand_8 (nand_8_out, S0, S0);
  nand nand_9 (nand_9_out, nand_1_out, S0, S1);
  nand nand_10 (nand_10_out, nand_2_out, S1, nand_3_out);
  nand nand_11 (nand_11_out, nand_4_out, nand_5_out, S0);
  nand nand_12 (nand_12_out, nand_6_out, nand_7_out, nand_8_out);
  nand nand_13 (nand_13_out, nand_9_out, nand_10_out, nand_11_out, nand_12_out);
  nand nand_14 (Y, nand_13_out, nand_13_out);
endmodule
